# Fritzing sketch Samuel's Project (saved by Fritzing 0.9.3b)
stripboards: 2

parts:
  VCC2 = Battery
  TP2 = TP4056 [chip_label=TP4056 package="DIP (Dual Inline) [THT]"]
  Buck_Convertor2 = Buck Convertor [part_number=LM2596 package=THT]
  M1 = 1 chan 5v relay module
  M2 = ZMPT101B Module [part_number=AC_Voltage_LM358_V3]
  OLED_I2C1 = OLED 128x64 I2C Monochrome Display
  LED2 = RGB LED (com. cathode, rbg) [package="5 mm [THT]"]
  R11 = Resistor [tolerance=±5% resistance=10k package=THT]
  R12 = Resistor [tolerance=±5% resistance=330 package=THT]
  R13 = Resistor [tolerance=±5% resistance=10k package=THT]
  L2 = sct-013 [part_number=sct-013 package="4Ucon 08780 [THT]"]
  C5 = Electrolytic Capacitor [capacitance=10µF package="100 mil [THT, electrolytic]"]
  J1 = Terminal Block - 2 pins [package=THT]
  J2 = Terminal Block - 2 pins [package=THT]
  U3 = ESP32-38PinWide [part_number=ESP32-38PinWide]

nets:
  N1: VCC2.-, TP2.pin5
  N2: VCC2.+, TP2.pin4
  N3: TP2.pin3, Buck_Convertor2.Positive_Input
  N4: TP2.pin6, Buck_Convertor2.Negative_Input
  GND: Buck_Convertor2.Negative_Output, M1.pin_2, M2.GND0, M2.GND1, OLED_I2C1.GND, LED2.common_cathode, R11.Pin_1, C5.-, U3.GND
  VCC: Buck_Convertor2.Positive_Output, M1.pin_1, M2.Vcc, R13.Pin_0, U3.VIN
  N5: M1.pin_3, U3.GPIO26
  N6: M1.pin_5, M2.AC-L, J1.Line_2
  N7: M1.pin_6, J2.Line_1
  N8: M2.Out, U3.GPIO34
  N9: M2.AC-N, J1.Line_1, J2.Line_2
  N10: OLED_I2C1.SDA, U3.GPIO21
  N11: OLED_I2C1.SCK, U3.GPIO22
  N12: OLED_I2C1.VDD, U3.3.3
  N13: LED2.red_anode, U3.GPIO25
  N14: LED2.blue_anode, U3.GPIO32
  N15: LED2.green_anode, U3.GPIO33
  N16: R11.Pin_0, R12.Pin_0, R13.Pin_1, L2.pin_0, C5.+
  N17: R12.Pin_1, L2.pin_1, U3.GPIO35

notes:
  Ensure LM2596 is tuned to 5v
  Use the 2s 4A chrging Module for Physical Hardware Connect the Battery -VE and Load -VE together same for the +VE pins
  Ensure this is 2s 3.7v and it full charged i.e 7.4v or 8v
  VCC-5v(ESP32)
  GND-GND(ESP32)
  Data Pin-GPIO35(ESP32)
  SSD1306 OLED:
  VCC-3.3v(ESP32)
  GND-GND(ESP32)
  SDA-GPIO21(ESP32)
  SCL-GPIO22(ESP32)
  10k
  330
  Incoming
  Supply
  Outgoing
  Supply
  ZMPT101B:
  VCC-5v(ESP32)
  GND-GND(ESP32)
  Data Pin-GPIO34(ESP32)
  Relay:
  VCC-5v(ESP32)
  GND-GND(ESP32)
  IN-GPIO34(ESP32)

custom parts:
  Battery: Your standard 2x 18650 battery pack (7.4 Volts)
  TP4056: A DIP stand-in part for whatever IC you want. With 6 pins on a 300mil dual inline package (DIP) footprint.
  Buck Convertor: DC to DC buck convertor
  1 chan 5v relay module: 1 Channel 5V Relay Module Board Shield with Optocoupler Support High and Low Level Trigger for Arduino.
  ZMPT101B Module: ZMPT101B Voltage Sensor Module This module uses a ZMPT101B voltage transformer and LM358 op amp to measure single phase voltages up to 250V. The module is powered by a 5V DC source and provides an analog output in the range 0–5V, proportional to the measured AC voltage. Links: ZMPT101B datasheet LM358 datasheet
  sct-013: sct-013 Current transformer. The pcb footprint is from the 3.5mm stereo jack (as the sensor comes with a 3.5 mm stero plug).
  Terminal Block - 2 pins: Generic Screw Terminal 8mm
  ESP32-38PinWide: Generic 38-Pin ESP32 with wide format (only access to one side of pins on a breadboard) based on Stephen Lilley's HiLetgo ESP-WROOM-32 ESP32 ESP-32S Development Board.
